# Fritzing sketch 4BitAdder (saved by Fritzing 0.9.10b)
breadboards: 2

parts:
  IC1 = DIP - 28 pins [chip_label=28C256 package="DIP (Dual Inline) [THT]"]
  Cfilter3 = Ceramic Capacitor [capacitance=1nF voltage=5V package="100 mil [THT, multilayer]"]
  R36 = Resistor [tolerance=±5% power=0.25 resistance=470k package=THT]
  Cfilter2 = Ceramic Capacitor [capacitance=1nF voltage=5V package="100 mil [THT, multilayer]"]
  Ct1 = Ceramic Capacitor [capacitance=1µF voltage=5V package="0603 [SMD, multilayer]"]
  R34 = Resistor [tolerance=±20% resistance=10k package="0805 [SMD]"]
  D2 = LED_BARGRAPH_10 [package=led_bargaph_10]
  Cctl1 = Ceramic Capacitor [capacitance=100nF voltage=5V package="0603 [SMD, multilayer]"]
  S3 = Pushbutton [package=THT]
  U5 = 555 Timer [package="DIP8 [THT]"]
  R33 = Resistor [tolerance=±20% resistance=1k package="0805 [SMD]"]
  LED3 = LED - 5mm [color="Green (555nm)" current=0.030 package="5 mm [THT]"]
  74LS2 = 74LS161 [chip_label=74LS161 package="DIP (Dual Inline) [THT]"]
  R35 = Resistor [tolerance=±20% resistance=10k package="0805 [SMD]"]
  S4 = Pushbutton [package="[THT]"]
  R42 = TRIMPOT [maximum_resistance=10kΩ knob_status=50% power=0.5W package=3386u]
  R43 = Resistor [tolerance=±20% resistance=220 package="0805 [SMD]"]
  Cfilter1 = Ceramic Capacitor [capacitance=10nF voltage=5V package="100 mil [THT, multilayer]"]
  R38 = Resistor [tolerance=±20% resistance=10k package="0805 [SMD]"]
  SW2 = DIP Switch 8 Position [package=dipswitch-08]
  R40 = Resistor [tolerance=±20% resistance=10k package="0805 [SMD]"]
  R39 = Resistor [tolerance=±20% resistance=10k package="0805 [SMD]"]
  Rpulldowns1 = Resistor [tolerance=±20% resistance=10k package="0805 [SMD]"]
  IC2 = 74LS02 [package=dil14]
  IC3 = DIP - 16 pins [chip_label=74LS173 package="DIP (Dual Inline) [THT]"]
  Part1 = 74LS86 [package="DIP14 [THT]"]
  74LS3 = 74LS283 [chip_label=74LS283 package="DIP (Dual Inline) [THT]"]
  IC4 = SELECTOR_MULTIPLEXER [package=dil16]

nets:
  GND: IC1.A14, IC1.A12, IC1.A7, IC1.A6, IC1.A5, IC1.A4, IC1.A3, IC1.!CE, IC1.A10, IC1.!OE, IC1.A11, IC1.A9, IC1.A8, IC1.A13, Cfilter2.1, Ct1.0, Cctl1.0, U5.Ground, LED3.cathode, 74LS2.GND, S4.Pin_3, S4.Pin_4, Cfilter1.0, R38.Pin_0, R40.Pin_0, R39.Pin_0, Rpulldowns1.Pin_0, IC2.GND, IC3.M, IC3.N, IC3.GND, Part1.GND, 74LS3.GND, IC4.A_1A, IC4.A_2A, IC4.P_GND, IC4.A_3A, IC4.A_4A
  N1: IC1.A2, D2.H_C
  N2: IC1.A1, D2.I_C
  N3: IC1.A0, D2.J_C, IC2.A2, IC2.B2
  N4: IC1.I/00, IC3.1D
  N5: IC1.I/01, IC3.2D
  N6: IC1.I/O2, IC3.3D
  N7: IC1.GND, Cfilter3.0
  N8: IC1.I/03, IC3.4D
  N9: IC1.I/O4, Part1.B1, Part1.B2, Part1.A3, Part1.A4, 74LS3.C0
  VCC: IC1.!WE, IC1.VCC, Cfilter3.1, Cfilter2.0, R34.Pin_1, S3.leg1, U5.Reset, U5.Vcc_Supply_Voltage, R33.Pin_0, 74LS2.VCC, Cfilter1.1, SW2.1, SW2.2, SW2.3, IC2.VCC, Part1.VCC, 74LS3.VCC, IC4.P_VCC
  N10: R36.Pin_0, U5.Output, 74LS2.CLK, IC3.CLK
  N11: R36.Pin_1, LED3.anode
  N12: Ct1.1, U5.Trigger
  N13: R34.Pin_0, 74LS2.ENP, 74LS2.-LOAD, 74LS2.ENT, S4.Pin_1, S4.Pin_2
  N14: D2.G_A, 74LS2.Out_4
  N15: D2.H_A, 74LS2.Out_3
  N16: D2.I_A, 74LS2.Out_2
  N17: D2.J_A, 74LS2.Out_1
  N18: D2.G_C, IC2.B1
  N19: Cctl1.1, U5.Control_Voltage
  N20: S3.leg0, IC2.A1, IC3.CLR
  N21: U5.Threshold, R43.Pin_0
  N22: U5.Discharge, R33.Pin_1, R35.Pin_0
  N23: 74LS2.-CLR, IC2.Y1
  N24: 74LS2.In_1, SW2.13, Rpulldowns1.Pin_1
  N25: 74LS2.In_2, SW2.14, R39.Pin_1
  N26: 74LS2.In_3, SW2.15, R40.Pin_1
  N27: 74LS2.In_4, R38.Pin_1, SW2.16
  N28: R35.Pin_1, R42.WIPER
  N29: R42.CW, R43.Pin_1
  N30: IC2.Y2, IC3.G1, IC3.G2, IC4.A_!A!_B
  N31: IC3.1Q, 74LS3.A1
  N32: IC3.2Q, 74LS3.A2
  N33: IC3.3Q, 74LS3.A3
  N34: IC3.4Q, 74LS3.A4
  N35: Part1.Y1, 74LS3.B1
  N36: Part1.Y2, 74LS3.B2
  N37: Part1.Y3, 74LS3.B3
  N38: Part1.Y4, 74LS3.B4
  N39: 74LS3.Sum2, IC4.A_2B
  N40: 74LS3.Sum1, IC4.A_1B
  N41: 74LS3.Sum4, IC4.A_4B
  N42: 74LS3.Sum3, IC4.A_3B

custom parts:
  DIP - 28 pins: A DIP stand-in part for whatever IC you want. With 28 pins on a 600mil dual inline package (DIP) footprint.
  74LS161: 74LS161 synchronous counter with asynchronous clear
  74LS02: 74LS02 Quad 2-input NOR
  DIP - 16 pins: A DIP stand-in part for whatever IC you want. With 16 pins on a 300mil dual inline package (DIP) footprint.
  74LS86: Quad 2-input XOR gate
  74LS283: 74LS283 4-bit full adder with fast carry. Inputs are A and B numbered with least significant bit 1 and most significant bit 4.
