# Fritzing sketch ClockedProgramCounter (saved by Fritzing 0.9.10b)
breadboards: 1

parts:
  Cfilter = Ceramic Capacitor [capacitance=10nF voltage=5V package="100 mil [THT, multilayer]"]
  U4 = 555 Timer [package="DIP8 [THT]"]
  R9 = Resistor [tolerance=±20% resistance=1k package="0805 [SMD]"]
  R10 = Resistor [tolerance=±20% resistance=10k package="0805 [SMD]"]
  R11 = Trimmer Potentiometer [maximum_resistance=1MΩ knob_status=50% power=0.5W package=THT]  # not connected
  Ct = Ceramic Capacitor [capacitance=1µF voltage=5V package="0603 [SMD, multilayer]"]
  Cctl = Ceramic Capacitor [capacitance=100nF voltage=5V package="0603 [SMD, multilayer]"]
  LED2 = LED - 5mm [color="Green (555nm)" current=0.030 package="5 mm [THT]"]
  R12 = Resistor [tolerance=±5% power=0.25 resistance=470k package=THT]
  R13 = Resistor [tolerance=±20% resistance=1M package="0805 [SMD]"]
  74LS1 = 74LS161 [chip_label=74LS161 package="DIP (Dual Inline) [THT]"]
  S1 = Pushbutton [package=THT]
  R14 = Resistor [tolerance=±20% resistance=10k package="0805 [SMD]"]
  Cfilter_2 = Ceramic Capacitor [capacitance=1nF voltage=5V package="100 mil [THT, multilayer]"]
  SW1 = DIP Switch 8 Position [package=dipswitch-08]
  D1 = LED_BARGRAPH_10 [package=led_bargaph_10]
  LED3 = LED - 5mm [color="Red (633nm)" current=0.030 package="5 mm [THT]"]
  LED4 = LED - 5mm [color="Red (633nm)" current=0.030 package="5 mm [THT]"]
  LED5 = LED - 5mm [color="Red (633nm)" current=0.030 package="5 mm [THT]"]
  LED6 = LED - 5mm [color="Red (633nm)" current=0.030 package="5 mm [THT]"]
  R15 = Resistor [tolerance=±20% resistance=1k package="0805 [SMD]"]
  R16 = Resistor [tolerance=±20% resistance=1k package="0805 [SMD]"]
  R17 = Resistor [tolerance=±20% resistance=1k package="0805 [SMD]"]
  R18 = Resistor [tolerance=±20% resistance=1k package="0805 [SMD]"]
  R19 = Resistor [tolerance=±20% resistance=1k package="0805 [SMD]"]
  Rpulldowns = Resistor [tolerance=±20% resistance=10k package="0805 [SMD]"]
  R21 = Resistor [tolerance=±20% resistance=10k package="0805 [SMD]"]
  R22 = Resistor [tolerance=±20% resistance=10k package="0805 [SMD]"]
  R23 = Resistor [tolerance=±20% resistance=10k package="0805 [SMD]"]
  R24 = Resistor [tolerance=±20% resistance=1k package="0805 [SMD]"]
  R25 = Resistor [tolerance=±20% resistance=1k package="0805 [SMD]"]
  R26 = Resistor [tolerance=±20% resistance=1k package="0805 [SMD]"]
  R27 = Resistor [tolerance=±20% resistance=1k package="0805 [SMD]"]

nets:
  N1: Cfilter.0, U4.Ground, Ct.0, Cctl.0, LED2.cathode, 74LS1.GND, S1.leg1, R15.Pin_0, R16.Pin_0, R17.Pin_0, R18.Pin_0, R19.Pin_0, Rpulldowns.Pin_0, R21.Pin_0, R22.Pin_0, R23.Pin_0, R24.Pin_1, R25.Pin_1, R26.Pin_1, R27.Pin_1
  N2: Cfilter.1, U4.Reset, U4.Vcc_Supply_Voltage, R9.Pin_0, 74LS1.VCC, R14.Pin_1, Cfilter_2.1, SW1.5, SW1.6, SW1.7, SW1.8
  N3: U4.Trigger, U4.Threshold, Ct.1, R13.Pin_0
  N4: U4.Output, R12.Pin_0, 74LS1.CLK
  N5: U4.Control_Voltage, Cctl.1
  N6: U4.Discharge, R9.Pin_1, R10.Pin_0
  N7: R10.Pin_1, R13.Pin_1
  N8: LED2.anode, R12.Pin_1
  N9: 74LS1.-CLR, S1.leg0, R14.Pin_0, Cfilter_2.0
  N10: 74LS1.In_1, SW1.12, D1.G_C, Rpulldowns.Pin_1
  N11: 74LS1.In_2, SW1.11, D1.H_C, R21.Pin_1
  N12: 74LS1.In_3, SW1.10, D1.I_C, R22.Pin_1
  N13: 74LS1.In_4, SW1.9, D1.J_C, R23.Pin_1
  N14: 74LS1.ENP, 74LS1.-LOAD, 74LS1.ENT, R19.Pin_1
  N15: 74LS1.Out_4, LED3.anode
  N16: 74LS1.Out_3, LED4.anode
  N17: 74LS1.Out_2, LED5.anode
  N18: 74LS1.Out_1, LED6.anode
  N19: D1.G_A, R24.Pin_0
  N20: D1.H_A, R26.Pin_0
  N21: D1.I_A, R25.Pin_0
  N22: D1.J_A, R27.Pin_0
  N23: D1.A_C, LED6.cathode, R15.Pin_1
  N24: LED3.cathode, R18.Pin_1
  N25: LED4.cathode, R17.Pin_1
  N26: LED5.cathode, R16.Pin_1

custom parts:
  74LS161: 74LS161 synchronous counter with asynchronous clear
