// Logisim project 4BitAdder.circ as structural Verilog: 1 circuit, main circuit main
module main (
);

  wire Clear_out, clock_1_out, n74157_1_pin1, n74157_1_pin2, n74157_1_pin3, n74157_1_pin4, n74157_1_pin5,
       n74157_1_pin6, n74157_1_pin7, n74157_1_pin9, n74157_1_pin10, n74157_1_pin11, n74157_1_pin12,
       n74157_1_pin13, n74157_1_pin14, n74161_1_pin7, n74283_1_pin2, n74283_1_pin6, n74283_1_pin11,
       n74283_1_pin15, nor_1_out;
  wire [3:0] n74161_1_pin14, n74283_1_pin5;
  wire [7:0] rom_1_data;

  Clock clock_1 (.out(clock_1_out));
  Button Clear (.out(Clear_out));
  nor nor_1 (nor_1_out, Clear_out, n74161_1_pin14[3]);
  _74161 u_74161_1 (
    .pin1(nor_1_out), .pin2(clock_1_out), .pin7(n74161_1_pin7), .pin14(n74161_1_pin14[0]),
    .pin13(n74161_1_pin14[1]), .pin12(n74161_1_pin14[2]), .pin11(n74161_1_pin14[3]), .pin10(n74161_1_pin7),
    .pin9(n74161_1_pin7));  // open: pin3, pin4, pin5, pin6, pin15
  LED led_1 (.in(n74157_1_pin12));
  LED led_2 (.in(n74157_1_pin9));
  LED led_3 (.in(n74157_1_pin7));
  LED led_4 (.in(n74157_1_pin4));
  _74157 u_74157_1 (
    .pin1(n74157_1_pin1), .pin2(n74157_1_pin2), .pin3(n74157_1_pin3), .pin4(n74157_1_pin4),
    .pin5(n74157_1_pin5), .pin6(n74157_1_pin6), .pin7(n74157_1_pin7), .pin14(n74157_1_pin14),
    .pin13(n74157_1_pin13), .pin12(n74157_1_pin12), .pin11(n74157_1_pin11), .pin10(n74157_1_pin10),
    .pin9(n74157_1_pin9));  // open: pin15
  ROM #(.addrWidth(4)) rom_1 (.addr(n74161_1_pin14), .data(rom_1_data));
  _74283 u_74283_1 (
    .pin1(n74157_1_pin5), .pin2(n74283_1_pin2), .pin3(n74283_1_pin5[1]), .pin4(n74157_1_pin2),
    .pin5(n74283_1_pin5[0]), .pin6(n74283_1_pin6), .pin7(rom_1_data[4]), .pin15(n74283_1_pin15),
    .pin14(n74283_1_pin5[2]), .pin13(n74157_1_pin11), .pin12(n74283_1_pin5[3]), .pin11(n74283_1_pin11),
    .pin10(n74157_1_pin14));  // open: pin9
  Register #(.width(4)) register_1 (
    .D(rom_1_data[3:0]), .en(n74157_1_pin1), .clk(clock_1_out), .Q(n74283_1_pin5), .clr(Clear_out));
  not not_1 (n74157_1_pin1, n74161_1_pin14[0]);
  _7486 u_7486_1 (
    .pin1(rom_1_data[0]), .pin2(rom_1_data[4]), .pin3(n74283_1_pin6), .pin4(rom_1_data[1]),
    .pin5(rom_1_data[4]), .pin6(n74283_1_pin2), .pin13(rom_1_data[4]), .pin12(rom_1_data[3]),
    .pin11(n74283_1_pin11), .pin10(rom_1_data[4]), .pin9(rom_1_data[2]), .pin8(n74283_1_pin15));
  // also tied to GND on the sheet: {n74157_1_pin10, n74157_1_pin13, n74157_1_pin6, n74157_1_pin3}
  // also tied to VCC on the sheet: n74161_1_pin7

  // Notes on the sheet:
  //   counter
  //   selector
  //   contents of rom_1 (hex, n*v repeats v):
  //   f7 15 f3 2 f3 a f3 12
  //   adder
  //   XOR
endmodule
