// Logisim project 8BitComputer.circ as structural Verilog: 7 circuits, main circuit main
module main (
  input  in_1
);

  wire and_1_out, clock_1_out, jumpopunit_1_jump, opcodedecoder_1_decsp, opcodedecoder_1_incsp,
       opcodedecoder_1_isjump, opcodedecoder_1_isramload, opcodedecoder_1_isramwrite,
       opcodedecoder_1_isrwrite;
  wire [3:0] registers_1_debugregistervalues_2, registers_1_debugregistervalues_3,
       registers_1_debugregistervalues_4, registers_1_debugregistervalues_5,
       registers_1_debugregistervalues_6;
  wire [7:0] alu_1_result, jumpopunit_1_jumplocation, memoryopunit_1_loadvalue, memoryopunit_1_ramaddress,
       opcodedecoder_1_value, programcounter_1_pc, ram_1_dout, registers_1_aout, registers_1_bout,
       registers_1_cout, registers_1_rspout;
  wire [31:0] rom_1_data;
  wire [59:0] registers_1_debugregistervalues;

  Clock clock_1 (.out(clock_1_out));
  Hex_Digit_Display hex_digit_display_1 (.value(registers_1_debugregistervalues[7:4]));  // open: dp
  Hex_Digit_Display hex_digit_display_2 (.value(registers_1_debugregistervalues[3:0]));  // open: dp
  Hex_Digit_Display hex_digit_display_3 (.value(registers_1_debugregistervalues[15:12]));  // open: dp
  ROM #(.dataWidth(32)) rom_1 (.addr(programcounter_1_pc), .data(rom_1_data));
  ProgramCounter programcounter_1 (
    .Clear(in_1), .Clock(clock_1_out), .LoadValue(opcodedecoder_1_value), .EnableLoad(and_1_out),
    .PC(programcounter_1_pc));
  RAM #(.asyncread("true")) ram_1 (
    .addr(memoryopunit_1_ramaddress), .we(opcodedecoder_1_isramwrite), .oe(opcodedecoder_1_isramload),
    .clk(clock_1_out), .din(opcodedecoder_1_value), .dout(ram_1_dout));
  Hex_Digit_Display hex_digit_display_4 (.value(registers_1_debugregistervalues[11:8]));  // open: dp
  Hex_Digit_Display hex_digit_display_5 (.value(registers_1_debugregistervalues[23:20]));  // open: dp
  Hex_Digit_Display hex_digit_display_6 (.value(registers_1_debugregistervalues[19:16]));  // open: dp
  Hex_Digit_Display hex_digit_display_7 (.value(registers_1_debugregistervalues[31:28]));  // open: dp
  Hex_Digit_Display hex_digit_display_8 (.value(registers_1_debugregistervalues[27:24]));  // open: dp
  Hex_Digit_Display hex_digit_display_9 (.value(registers_1_debugregistervalues[39:36]));  // open: dp
  Hex_Digit_Display hex_digit_display_10 (.value(registers_1_debugregistervalues[35:32]));  // open: dp
  Hex_Digit_Display hex_digit_display_11 (.value(registers_1_debugregistervalues_3));  // open: dp
  Hex_Digit_Display hex_digit_display_12 (.value(registers_1_debugregistervalues_2));  // open: dp
  Hex_Digit_Display hex_digit_display_13 (.value(registers_1_debugregistervalues_5));  // open: dp
  Hex_Digit_Display hex_digit_display_14 (.value(registers_1_debugregistervalues_4));  // open: dp
  Hex_Digit_Display hex_digit_display_15 (.value(registers_1_debugregistervalues_6));  // open: dp
  Hex_Digit_Display hex_digit_display_16 (.value(registers_1_debugregistervalues[59:56]));  // open: dp
  Registers registers_1 (
    .WriteEnable(opcodedecoder_1_isrwrite), .Value(opcodedecoder_1_value), .Clock(clock_1_out), .Clear(in_1),
    .Aaddress(rom_1_data[23:16]), .Baddress(rom_1_data[15:8]), .Caddress(rom_1_data[7:0]),
    .IncSP(opcodedecoder_1_incsp), .DecSP(opcodedecoder_1_decsp), .Aout(registers_1_aout),
    .Bout(registers_1_bout), .Cout(registers_1_cout), .RSPout(registers_1_rspout),
    .DebugRegisterValues({registers_1_debugregistervalues_6, registers_1_debugregistervalues[59:56], registers_1_debugregistervalues_5, registers_1_debugregistervalues_4, registers_1_debugregistervalues_3, registers_1_debugregistervalues_2, registers_1_debugregistervalues[39:0]}));
  ALU alu_1 (.OpCode(rom_1_data[31:24]), .RB(registers_1_bout), .RC(registers_1_cout), .Result(alu_1_result));
  MemoryOpUnit memoryopunit_1 (
    .OpCode(rom_1_data[31:24]), .RSP(registers_1_rspout), .RA(registers_1_aout), .RB(registers_1_bout),
    .A(rom_1_data[23:16]), .B(rom_1_data[15:8]), .RAMVal(ram_1_dout), .loadValue(memoryopunit_1_loadvalue),
    .RAMAddress(memoryopunit_1_ramaddress));
  JumpOpUnit jumpopunit_1 (
    .OpCode(rom_1_data[31:24]), .RA(registers_1_aout), .RB(registers_1_bout), .A(rom_1_data[23:16]),
    .Jump(jumpopunit_1_jump), .JumpLocation(jumpopunit_1_jumplocation));
  OpcodeDecoder opcodedecoder_1 (
    .OpCode(rom_1_data[31:24]), .ALUResult(alu_1_result), .MemoryOut(memoryopunit_1_loadvalue),
    .JumpLocation(jumpopunit_1_jumplocation), .IsRWrite(opcodedecoder_1_isrwrite),
    .IsJump(opcodedecoder_1_isjump), .IsRAMLoad(opcodedecoder_1_isramload),
    .IsRAMWrite(opcodedecoder_1_isramwrite), .DecSP(opcodedecoder_1_decsp), .IncSP(opcodedecoder_1_incsp),
    .Value(opcodedecoder_1_value));
  and and_1 (and_1_out, jumpopunit_1_jump, opcodedecoder_1_isjump);

  // Notes on the sheet:
  //   R0
  //   R1
  //   contents of rom_1 (hex, n*v repeats v):
  //   0 400001ff 4001ffff 410201ff 440500ff 450001ff 46ff01ff 4700ffff
  //   R2
  //   R3
  //   R4
  //   R5
  //   R6
  //   RSP
endmodule

module ProgramCounter (
  input  Clear,
  input  Clock,
  input  [7:0] LoadValue,
  input  EnableLoad,
  output [7:0] PC
);

  wire n74161_1_pin1, n74161_1_pin15, n74161_2_pin1, not_1_out;

  not not_1 (not_1_out, EnableLoad);
  _74161 u_74161_1 (
    .pin1(n74161_1_pin1), .pin2(Clock), .pin3(LoadValue[0]), .pin4(LoadValue[1]), .pin5(LoadValue[2]),
    .pin6(LoadValue[3]), .pin7(not_1_out), .pin15(n74161_1_pin15), .pin14(PC[0]), .pin13(PC[1]),
    .pin12(PC[2]), .pin11(PC[3]), .pin10(not_1_out), .pin9(not_1_out));
  not not_2 (n74161_1_pin1, Clear);
  _74161 u_74161_2 (
    .pin1(n74161_2_pin1), .pin2(n74161_1_pin15), .pin3(LoadValue[4]), .pin4(LoadValue[5]),
    .pin5(LoadValue[6]), .pin6(LoadValue[7]), .pin7(not_1_out), .pin14(PC[4]), .pin13(PC[5]), .pin12(PC[6]),
    .pin11(PC[7]), .pin10(not_1_out), .pin9(not_1_out));  // open: pin15
  not not_3 (n74161_2_pin1, Clear);
endmodule

module OpcodeDecoder (
  input  [7:0] OpCode,
  input  [7:0] ALUResult,
  input  [7:0] MemoryOut,
  input  [7:0] JumpLocation,
  output IsRWrite,
  output IsJump,
  output IsRAMLoad,
  output IsRAMWrite,
  output DecSP,
  output IncSP,
  output [7:0] Value
);

  wire and_1_out, and_2_out, and_4_out, and_7_out, or_1_out, xor_1_out;
  wire [7:0] multiplexer_1_out;

  xor xor_1 (xor_1_out, OpCode[4], OpCode[5]);
  and and_1 (and_1_out, ~OpCode[4], ~OpCode[5], OpCode[6]);  // AND_Gate
  and and_2 (and_2_out, xor_1_out, ~OpCode[6]);  // AND_Gate
  and and_3 (IsJump, OpCode[4], OpCode[5], ~OpCode[6]);  // AND_Gate
  Multiplexer #(.width(8)) multiplexer_1 (.in0(ALUResult), .in1(MemoryOut), .out(multiplexer_1_out), .sel(and_1_out));
  or or_1 (or_1_out, and_1_out, and_2_out);
  and and_4 (and_4_out, and_1_out, OpCode[1], ~OpCode[2]);  // AND_Gate
  and and_5 (DecSP, OpCode[2], OpCode[1], ~OpCode[0]);  // AND_Gate
  and and_6 (IncSP, and_1_out, OpCode[2], OpCode[1], OpCode[0]);
  Multiplexer #(.width(8)) multiplexer_2 (.in0(multiplexer_1_out), .in1(JumpLocation), .out(Value), .sel(IsJump));
  and and_7 (and_7_out, or_1_out, ~OpCode[2]);  // AND_Gate
  or or_2 (IsRWrite, and_7_out, IncSP);
  or or_3 (IsRAMLoad, and_4_out, IncSP);
  xor xor_2 (IsRAMWrite, OpCode[2], IncSP);

  // Notes on the sheet:
  //   IsMemoryOp
  //   IsALUOp
endmodule

module Registers (
  input  WriteEnable,
  input  [7:0] Value,
  input  Clock,
  input  Clear,
  input  [7:0] Aaddress,
  input  [7:0] Baddress,
  input  [7:0] Caddress,
  input  IncSP,
  input  DecSP,
  output [7:0] Aout,
  output [7:0] Bout,
  output [7:0] Cout,
  output [7:0] RSPout,
  output [63:0] DebugRegisterValues
);

  wire decoder_1_out0, decoder_1_out1, decoder_1_out2, decoder_1_out3, decoder_1_out4, decoder_1_out5,
       decoder_1_out6;
  wire [7:0] adder_1_out, multiplexer_1_out, multiplexer_2_out, subtractor_1_out;

  Adder adder_1 (.a(DebugRegisterValues[63:56]), .b(8'h1), .out(adder_1_out));  // open: cin, cout
  Subtractor subtractor_1 (.a(DebugRegisterValues[63:56]), .b(8'h1), .out(subtractor_1_out));  // open: bin, bout
  Multiplexer #(.select(2), .width(8)) multiplexer_1 (
    .in0(DebugRegisterValues[63:56]), .in1(adder_1_out), .in2(subtractor_1_out), .out(multiplexer_1_out),
    .sel({DecSP, IncSP}));  // open: in3
  Multiplexer #(.width(8)) multiplexer_2 (
    .in0(multiplexer_1_out), .in1({8{1'b1}}), .out(multiplexer_2_out), .sel(Clear));
  Decoder #(.select(3)) decoder_1 (
    .out0(decoder_1_out0), .out1(decoder_1_out1), .out2(decoder_1_out2), .out3(decoder_1_out3),
    .out4(decoder_1_out4), .out5(decoder_1_out5), .out6(decoder_1_out6), .sel(Aaddress[2:0]), .en(WriteEnable));  // open: out7
  Register RSP (.D(multiplexer_2_out), .en(Clock), .Q(DebugRegisterValues[63:56]), .clk(Clock));  // open: clr
  Register R6 (.D(Value), .en(decoder_1_out6), .Q(DebugRegisterValues[55:48]), .clk(Clock), .clr(Clear));
  Register R5 (.D(Value), .en(decoder_1_out5), .Q(DebugRegisterValues[47:40]), .clk(Clock), .clr(Clear));
  Register R4 (.D(Value), .en(decoder_1_out4), .Q(DebugRegisterValues[39:32]), .clk(Clock), .clr(Clear));
  Register R3 (.D(Value), .en(decoder_1_out3), .Q(DebugRegisterValues[31:24]), .clk(Clock), .clr(Clear));
  Register R2 (.D(Value), .en(decoder_1_out2), .Q(DebugRegisterValues[23:16]), .clk(Clock), .clr(Clear));
  Register R1 (.D(Value), .en(decoder_1_out1), .Q(DebugRegisterValues[15:8]), .clk(Clock), .clr(Clear));
  Register R0 (.D(Value), .en(decoder_1_out0), .Q(DebugRegisterValues[7:0]), .clk(Clock), .clr(Clear));
  Multiplexer #(.select(3), .width(8)) multiplexer_3 (
    .in0(DebugRegisterValues[7:0]), .in1(DebugRegisterValues[15:8]), .in2(DebugRegisterValues[23:16]),
    .in3(DebugRegisterValues[31:24]), .in4(DebugRegisterValues[39:32]), .in5(DebugRegisterValues[47:40]),
    .in6(DebugRegisterValues[55:48]), .out(Aout), .sel(Aaddress[2:0]));  // open: in7
  Multiplexer #(.select(3), .width(8)) multiplexer_4 (
    .in0(DebugRegisterValues[7:0]), .in1(DebugRegisterValues[15:8]), .in2(DebugRegisterValues[23:16]),
    .in3(DebugRegisterValues[31:24]), .in4(DebugRegisterValues[39:32]), .in5(DebugRegisterValues[47:40]),
    .in6(DebugRegisterValues[55:48]), .out(Bout), .sel(Baddress[2:0]));  // open: in7
  Multiplexer #(.select(3), .width(8)) multiplexer_5 (
    .in0(DebugRegisterValues[7:0]), .in1(DebugRegisterValues[15:8]), .in2(DebugRegisterValues[23:16]),
    .in3(DebugRegisterValues[31:24]), .in4(DebugRegisterValues[39:32]), .in5(DebugRegisterValues[47:40]),
    .in6(DebugRegisterValues[55:48]), .out(Cout), .sel(Caddress[2:0]));  // open: in7

  assign RSPout = DebugRegisterValues[63:56];
endmodule

module ALU (
  input  [7:0] OpCode,
  input  [7:0] RB,
  input  [7:0] RC,
  output [7:0] Result
);

  wire and_2_out, and_3_out, and_4_out, and_5_out, and_6_out, and_7_out, and_8_out, and_9_out, and_10_out,
       and_11_out, and_12_out, and_13_out, and_14_out, and_15_out, and_16_out, and_26_out, and_27_out,
       and_28_out, comparator_1_eq, comparator_1_gt, comparator_1_lt, comparator_2_eq, comparator_2_gt,
       comparator_2_lt, not_6_out, not_7_out, not_8_out, not_9_out, or_4_out, or_5_out, or_6_out, or_7_out,
       xor_4_out, xor_5_out, xor_6_out;
  wire [5:0] undriven_3;
  wire [7:0] adder_1_out, adder_2_out, adder_3_out, and_1_out, and_17_out, and_18_out, and_19_out,
       and_20_out, and_21_out, and_22_out, and_23_out, and_24_out, and_25_out, bit_extender_1_out,
       bit_extender_2_out, bit_extender_3_out, bit_extender_4_out, bit_extender_5_out, bit_extender_6_out,
       bit_extender_7_out, bit_extender_8_out, bit_extender_9_out, bit_extender_10_out, bit_extender_11_out,
       bit_extender_12_out, bit_extender_13_out, divider_1_out, divider_1_rem, divider_2_out, divider_2_rem,
       multiplexer_1_out, multiplexer_3_out, multiplier_1_out, multiplier_2_out, not_1_out, not_2_out,
       not_3_out, not_4_out, not_5_out, not_10_out, or_1_out, or_2_out, or_3_out, undriven, undriven_2,
       xor_1_out, xor_2_out, xor_3_out;

  Adder adder_1 (.a(RB), .b(RC), .out(adder_1_out));  // open: cin, cout
  Adder adder_2 (.a(RB), .b(not_1_out), .out(adder_2_out), .cin(1'b1));  // open: cout
  assign not_1_out = ~RC;  // NOT_Gate not_1, 8 bits wide
  Multiplier multiplier_1 (.a(RB), .b(RC), .out(multiplier_1_out));  // open: cin, cout
  Divider divider_1 (.a(RB), .b(RC), .out(divider_1_out), .rem(divider_1_rem));  // open: upper
  assign not_2_out = ~RB;  // NOT_Gate not_2, 8 bits wide
  assign and_1_out = RB & RC;  // AND_Gate and_1, 8 bits wide
  assign or_1_out = RB | RC;  // OR_Gate or_1, 8 bits wide
  assign xor_1_out = RB ^ RC;  // XOR_Gate xor_1, 8 bits wide
  Comparator comparator_1 (.a(RB), .b(RC), .gt(comparator_1_gt), .eq(comparator_1_eq), .lt(comparator_1_lt));
  assign not_3_out = ~bit_extender_2_out;  // NOT_Gate not_3, 8 bits wide
  assign not_4_out = ~bit_extender_3_out;  // NOT_Gate not_4, 8 bits wide
  assign bit_extender_1_out = {{7{comparator_1_gt}}, comparator_1_gt};  // Bit_Extender bit_extender_1
  assign bit_extender_2_out = {{7{comparator_1_eq}}, comparator_1_eq};  // Bit_Extender bit_extender_2
  assign bit_extender_3_out = {{7{comparator_1_lt}}, comparator_1_lt};  // Bit_Extender bit_extender_3
  assign not_5_out = ~bit_extender_1_out;  // NOT_Gate not_5, 8 bits wide
  Multiplexer #(.select(3), .width(8)) multiplexer_1 (
    .in0(adder_1_out), .in1(adder_2_out), .in2(multiplier_1_out), .in3(divider_1_out), .in4(divider_1_rem),
    .out(multiplexer_1_out), .sel(OpCode[2:0]));  // open: in5, in6, in7
  Multiplexer #(.select(2), .width(8)) multiplexer_2 (
    .in1(multiplexer_1_out), .in2(multiplexer_3_out), .out(Result), .sel(OpCode[5:4]));  // open: in0, in3
  Multiplexer #(.select(4), .width(8)) multiplexer_3 (
    .in0(not_2_out), .in1(and_1_out), .in2(or_1_out), .in3(xor_1_out), .in4(bit_extender_2_out),
    .in5(not_3_out), .in6(not_4_out), .in7(not_5_out), .in8(bit_extender_1_out), .in9(bit_extender_3_out),
    .out(multiplexer_3_out), .sel(OpCode[3:0]));  // open: in10, in11, in12, in13, in14, in15
  not not_6 (not_6_out, undriven_3[3]);
  not not_7 (not_7_out, undriven_3[2]);
  not not_8 (not_8_out, undriven_3[1]);
  not not_9 (not_9_out, undriven_3[0]);
  and and_2 (and_2_out, not_9_out, not_8_out, not_7_out, undriven_3[4]);
  and and_3 (and_3_out, undriven_3[0], not_8_out, undriven_3[4]);
  and and_4 (and_4_out, undriven_3[1], not_9_out, undriven_3[4]);
  and and_5 (and_5_out, undriven_3[1], undriven_3[0], undriven_3[4]);
  and and_6 (and_6_out, undriven_3[2], undriven_3[4]);
  and and_7 (and_7_out, not_9_out, not_8_out, not_7_out, not_6_out, undriven_3[5]);
  and and_8 (and_8_out, undriven_3[0], not_8_out, not_7_out, not_6_out, undriven_3[5]);
  and and_9 (and_9_out, undriven_3[1], not_9_out, not_7_out, undriven_3[5]);
  and and_10 (and_10_out, undriven_3[1], undriven_3[0], not_7_out, undriven_3[5]);
  and and_11 (and_11_out, undriven_3[2], not_9_out, not_8_out, undriven_3[5]);
  and and_12 (and_12_out, undriven_3[2], undriven_3[0], not_8_out);
  and and_13 (and_13_out, undriven_3[2], undriven_3[1], not_9_out);
  and and_14 (and_14_out, undriven_3[2], undriven_3[1], undriven_3[0]);
  and and_15 (and_15_out, undriven_3[3], not_9_out);
  and and_16 (and_16_out, undriven_3[3], undriven_3[0]);
  assign bit_extender_4_out = {{7{and_2_out}}, and_2_out};  // Bit_Extender bit_extender_4
  assign or_2_out = bit_extender_4_out | bit_extender_5_out;  // OR_Gate or_2, 8 bits wide
  assign bit_extender_5_out = {{7{and_3_out}}, and_3_out};  // Bit_Extender bit_extender_5
  assign bit_extender_6_out = {{7{and_4_out}}, and_4_out};  // Bit_Extender bit_extender_6
  assign bit_extender_7_out = {{7{and_5_out}}, and_5_out};  // Bit_Extender bit_extender_7
  assign bit_extender_8_out = {{7{and_6_out}}, and_6_out};  // Bit_Extender bit_extender_8
  assign bit_extender_9_out = {{7{and_7_out}}, and_7_out};  // Bit_Extender bit_extender_9
  assign bit_extender_10_out = {{7{and_8_out}}, and_8_out};  // Bit_Extender bit_extender_10
  assign bit_extender_11_out = {{7{and_9_out}}, and_9_out};  // Bit_Extender bit_extender_11
  assign bit_extender_12_out = {{7{and_10_out}}, and_10_out};  // Bit_Extender bit_extender_12
  Adder adder_3 (.a(undriven), .b(xor_2_out), .out(adder_3_out), .cin(and_3_out));  // open: cout
  assign xor_2_out = undriven_2 ^ bit_extender_5_out;  // XOR_Gate xor_2, 8 bits wide
  Multiplier multiplier_2 (.a(undriven), .b(undriven_2), .out(multiplier_2_out));  // open: cin, cout
  Divider divider_2 (.a(undriven), .b(undriven_2), .out(divider_2_out), .rem(divider_2_rem));  // open: upper
  assign not_10_out = ~undriven;  // NOT_Gate not_10, 8 bits wide
  assign and_17_out = undriven & undriven_2;  // AND_Gate and_17, 8 bits wide
  assign or_3_out = undriven | undriven_2;  // OR_Gate or_3, 8 bits wide
  assign xor_3_out = undriven ^ undriven_2;  // XOR_Gate xor_3, 8 bits wide
  or or_4 (or_4_out, and_15_out, and_14_out);
  xor xor_4 (xor_4_out, and_14_out, comparator_2_gt);
  or or_5 (or_5_out, and_11_out, and_12_out);
  xor xor_5 (xor_5_out, and_12_out, comparator_2_eq);
  Comparator comparator_2 (
    .a(undriven), .b(undriven_2), .gt(comparator_2_gt), .eq(comparator_2_eq), .lt(comparator_2_lt));
  xor xor_6 (xor_6_out, comparator_2_lt, and_13_out);
  or or_6 (or_6_out, and_13_out, and_16_out);
  assign and_18_out = or_2_out & adder_3_out;  // AND_Gate and_18, 8 bits wide
  assign and_19_out = bit_extender_6_out & multiplier_2_out;  // AND_Gate and_19, 8 bits wide
  assign and_20_out = bit_extender_7_out & divider_2_out;  // AND_Gate and_20, 8 bits wide
  assign and_21_out = divider_2_rem & bit_extender_8_out;  // AND_Gate and_21, 8 bits wide
  assign and_22_out = bit_extender_9_out & not_10_out;  // AND_Gate and_22, 8 bits wide
  assign and_23_out = bit_extender_10_out & and_17_out;  // AND_Gate and_23, 8 bits wide
  assign and_24_out = bit_extender_11_out & or_3_out;  // AND_Gate and_24, 8 bits wide
  assign and_25_out = bit_extender_12_out & xor_3_out;  // AND_Gate and_25, 8 bits wide
  and and_26 (and_26_out, or_4_out, xor_4_out);
  and and_27 (and_27_out, or_5_out, xor_5_out);
  and and_28 (and_28_out, xor_6_out, or_6_out);
  assign bit_extender_13_out = {{7{or_7_out}}, or_7_out};  // Bit_Extender bit_extender_13
  or or_7 (or_7_out, and_26_out, and_27_out, and_28_out);
  // OR_Gate or_8 has open pins: in0=and_18_out, in1=and_19_out, in2=and_20_out, in3=and_21_out, in4=and_22_out, in5=and_23_out, in6=and_24_out, in7=and_25_out, in8=bit_extender_13_out, out=open

  // Notes on the sheet:
  //   Old version of ALU (I forgot multiplexers were a thing)
endmodule

module MemoryOpUnit (
  input  [7:0] OpCode,
  input  [7:0] RSP,
  input  [7:0] RA,
  input  [7:0] RB,
  input  [7:0] A,
  input  [7:0] B,
  input  [7:0] RAMVal,
  output [7:0] loadValue,
  output [7:0] RAMAddress
);

  wire [7:0] adder_1_out;

  Adder adder_1 (.a(RSP), .b(8'h1), .out(adder_1_out));  // open: cin, cout
  Multiplexer #(.select(3), .width(8)) multiplexer_1 (
    .in0(B), .in1(RB), .in2(RAMVal), .in3(RAMVal), .in4(RB), .in5(RB), .in6(RB), .in7(RAMVal),
    .out(loadValue), .sel(OpCode[2:0]));
  Multiplexer #(.select(3), .width(8)) multiplexer_2 (
    .in2(B), .in3(RB), .in4(A), .in5(RA), .in6(RSP), .in7(adder_1_out), .out(RAMAddress), .sel(OpCode[2:0]));  // open: in0, in1
endmodule

module JumpOpUnit (
  input  [7:0] OpCode,
  input  [7:0] RA,
  input  [7:0] RB,
  input  [7:0] A,
  output Jump,
  output [7:0] JumpLocation
);

  wire and_1_out, or_1_out;

  or or_1 (or_1_out, RB[0], RB[1], RB[2], RB[3], RB[4], RB[5], RB[6], RB[7]);
  Multiplexer #(.width(8)) multiplexer_1 (.in0(A), .in1(RA), .out(JumpLocation), .sel(OpCode[0]));
  or or_2 (Jump, ~OpCode[1], and_1_out);  // OR_Gate
  and and_1 (and_1_out, OpCode[1], or_1_out);

  // Notes on the sheet:
  //   (indirect location)
  //   (condition)
  //   (location)
  //   0x30 JMP    (JMP     Address     _               _)
  //   0x31 JMPi   (JMPi    Rloc           _                _)
  //   0x32 JMPT  (JMPT  Address   Rcondition _)
  //   0x33 JMPTi (JMPTi Rlocation Rcondition _)
endmodule
