// Logisim project MiniALU.circ as structural Verilog: 3 circuits, main circuit main
module OpcodeDecoder (
  input  [7:0] Opcode,
  output NOP,
  output ADD,
  output SUB,
  output MUL,
  output DIV,
  output MODx,
  output NOTx,
  output ANDx,
  output ORx,
  output XORx,
  output EQ,
  output NEQ,
  output GTE,
  output LTE,
  output GT,
  output LT,
  output JMP,
  output JMPi,
  output JMPT,
  output JMPTi,
  output SET,
  output COPY,
  output LOAD,
  output LOADi,
  output STR,
  output STRi,
  output PUSH,
  output POP
);

  wire decoder_1_out0, decoder_1_out1, decoder_1_out2, decoder_1_out3, decoder_1_out4, nor_1_out, nor_2_out;

  Decoder #(.enable("false"), .select(3)) decoder_1 (
    .out0(decoder_1_out0), .out1(decoder_1_out1), .out2(decoder_1_out2), .out3(decoder_1_out3),
    .out4(decoder_1_out4), .sel(Opcode[6:4]));  // open: out5, out6, out7
  Demultiplexer #(.select(3)) demultiplexer_1 (
    .out0(ADD), .out1(SUB), .out2(MUL), .out3(DIV), .out4(MODx), .in(decoder_1_out1), .sel(Opcode[2:0]));  // open: out5, out6, out7
  Demultiplexer #(.select(4)) demultiplexer_2 (
    .out0(NOTx), .out1(ANDx), .out2(ORx), .out3(XORx), .out4(EQ), .out5(NEQ), .out6(GTE), .out7(LTE),
    .out8(GT), .out9(LT), .in(decoder_1_out2), .sel(Opcode[3:0]));  // open: out10, out11, out12, out13, out14, out15
  Demultiplexer #(.select(2)) demultiplexer_3 (
    .out0(JMP), .out1(JMPi), .out2(JMPT), .out3(JMPTi), .in(decoder_1_out3), .sel(Opcode[1:0]));
  Demultiplexer #(.select(3)) demultiplexer_4 (
    .out0(SET), .out1(COPY), .out2(LOAD), .out3(LOADi), .out4(STR), .out5(STRi), .out6(PUSH), .out7(POP),
    .in(decoder_1_out4), .sel(Opcode[2:0]));
  nor nor_1 (nor_1_out, Opcode[0], Opcode[1]);
  nor nor_2 (nor_2_out, Opcode[2], Opcode[3]);
  and and_1 (NOP, nor_1_out, nor_2_out, decoder_1_out0);
endmodule

module ALU (
  input  [7:0] A,
  input  [7:0] B,
  input  ADD,
  input  SUB,
  input  MUL,
  input  DIV,
  input  MODx,
  input  NOTx,
  input  ANDx,
  input  ORx,
  input  XORx,
  input  EQ,
  input  NEQ,
  input  GTE,
  input  LTE,
  input  GT,
  input  LT,
  output [7:0] Result
);

  wire and_9_out, and_10_out, and_11_out, comparator_1_eq, comparator_1_gt, comparator_1_lt, or_1_out,
       or_3_out, or_4_out, or_5_out, or_6_out, xor_3_out;
  wire [7:0] adder_1_out, and_1_out, and_2_out, and_3_out, and_4_out, and_5_out, and_6_out, and_7_out,
       and_8_out, and_12_out, bit_extender_1_out, bit_extender_2_out, bit_extender_3_out, bit_extender_4_out,
       bit_extender_5_out, bit_extender_6_out, bit_extender_7_out, bit_extender_8_out, bit_extender_9_out,
       bit_extender_10_out, divider_1_out, divider_1_rem, multiplier_1_out, not_1_out, or_2_out, xor_1_out,
       xor_2_out;

  or or_1 (or_1_out, ADD, SUB);
  Comparator comparator_1 (.a(A), .b(B), .gt(comparator_1_gt), .eq(comparator_1_eq), .lt(comparator_1_lt));
  assign bit_extender_1_out = {{7{MUL}}, MUL};  // Bit_Extender bit_extender_1
  Multiplier multiplier_1 (.a(A), .b(B), .out(multiplier_1_out));  // open: cin, cout
  assign bit_extender_2_out = {{7{DIV}}, DIV};  // Bit_Extender bit_extender_2
  Divider divider_1 (.a(A), .b(B), .out(divider_1_out), .rem(divider_1_rem));  // open: upper
  assign bit_extender_3_out = {{7{MODx}}, MODx};  // Bit_Extender bit_extender_3
  assign bit_extender_4_out = {{7{NOTx}}, NOTx};  // Bit_Extender bit_extender_4
  assign not_1_out = ~A;  // NOT_Gate not_1, 8 bits wide
  assign bit_extender_5_out = {{7{ANDx}}, ANDx};  // Bit_Extender bit_extender_5
  assign and_1_out = A & B;  // AND_Gate and_1, 8 bits wide
  assign bit_extender_6_out = {{7{ORx}}, ORx};  // Bit_Extender bit_extender_6
  assign or_2_out = A | B;  // OR_Gate or_2, 8 bits wide
  assign bit_extender_7_out = {{7{EQ}}, EQ};  // Bit_Extender bit_extender_7
  assign xor_1_out = A ^ B;  // XOR_Gate xor_1, 8 bits wide
  assign xor_2_out = B ^ bit_extender_8_out;  // XOR_Gate xor_2, 8 bits wide
  assign bit_extender_8_out = {{7{SUB}}, SUB};  // Bit_Extender bit_extender_8
  xor xor_3 (xor_3_out, EQ, comparator_1_eq);
  or or_3 (or_3_out, EQ, EQ, EQ);
  or or_4 (or_4_out, EQ, EQ);
  or or_5 (or_5_out, EQ, EQ);
  assign and_2_out = bit_extender_1_out & multiplier_1_out;  // AND_Gate and_2, 8 bits wide
  assign and_3_out = bit_extender_2_out & divider_1_out;  // AND_Gate and_3, 8 bits wide
  assign and_4_out = divider_1_rem & bit_extender_3_out;  // AND_Gate and_4, 8 bits wide
  assign and_5_out = bit_extender_4_out & not_1_out;  // AND_Gate and_5, 8 bits wide
  assign and_6_out = bit_extender_5_out & and_1_out;  // AND_Gate and_6, 8 bits wide
  assign and_7_out = bit_extender_6_out & or_2_out;  // AND_Gate and_7, 8 bits wide
  assign and_8_out = bit_extender_7_out & xor_1_out;  // AND_Gate and_8, 8 bits wide
  assign bit_extender_9_out = {{7{or_1_out}}, or_1_out};  // Bit_Extender bit_extender_9
  Adder adder_1 (.a(A), .b(xor_2_out), .out(adder_1_out), .cin(SUB));  // open: cout
  and and_9 (and_9_out, or_4_out, comparator_1_gt);
  and and_10 (and_10_out, or_3_out, xor_3_out);
  and and_11 (and_11_out, comparator_1_lt, or_5_out);
  assign and_12_out = bit_extender_9_out & adder_1_out;  // AND_Gate and_12, 8 bits wide
  assign bit_extender_10_out = {{7{or_6_out}}, or_6_out};  // Bit_Extender bit_extender_10
  or or_6 (or_6_out, and_9_out, and_10_out, and_11_out);
  assign Result = and_12_out | bit_extender_10_out | and_2_out | and_3_out | and_4_out | and_5_out | and_6_out | and_7_out | and_8_out;  // OR_Gate or_7, 8 bits wide

  assign GT = EQ;
  assign GTE = EQ;
  assign LT = EQ;
  assign LTE = EQ;
  assign NEQ = EQ;
  assign XORx = EQ;

  // Notes on the sheet:
  //   EQ / LTE / GTE
  //   GT / GTE
  //   LT / LTE
endmodule

module main (
  input  [7:0] in_1,
  input  [7:0] in_2,
  input  [7:0] in_3,
  input  [7:0] in_4,
  input  [7:0] in_5,
  input  [7:0] in_6,
  input  [7:0] in_7,
  input  [7:0] in_8,
  input  clear,
  input  enableLoad_activeLow
);

  wire buffer_1_out, clock_1_out, dipswitch_1_sw1, dipswitch_1_sw2, dipswitch_1_sw3, dipswitch_1_sw4,
       n74161_1_pin1, opcodedecoder_1_add, opcodedecoder_1_andx, opcodedecoder_1_div, opcodedecoder_1_eq,
       opcodedecoder_1_gt, opcodedecoder_1_gte, opcodedecoder_1_lt, opcodedecoder_1_lte,
       opcodedecoder_1_modx, opcodedecoder_1_mul, opcodedecoder_1_neq, opcodedecoder_1_notx,
       opcodedecoder_1_orx, opcodedecoder_1_sub, opcodedecoder_1_xorx;
  wire [3:0] multiplexer_1_out, multiplexer_1_out_2, multiplexer_2_out, multiplexer_2_out_2, n74161_1_pin14,
       register_1_q;
  wire [7:0] alu_1_result, multiplexer_3_out, R0_q, R1_q, R2_q, R3_q, R4_q, R5_q, R6_q, R7_q, rom_1_data,
       rom_1_data_2, rom_1_data_3;
  wire [31:24] rom_1_data_4;

  DipSwitch #(.number(4)) dipswitch_1 (
    .sw1(dipswitch_1_sw1), .sw2(dipswitch_1_sw2), .sw3(dipswitch_1_sw3), .sw4(dipswitch_1_sw4));
  Clock clock_1 (.out(clock_1_out));
  _74161 u_74161_1 (
    .pin1(n74161_1_pin1), .pin2(clock_1_out), .pin3(dipswitch_1_sw4), .pin4(dipswitch_1_sw3),
    .pin5(dipswitch_1_sw2), .pin6(dipswitch_1_sw1), .pin7(enableLoad_activeLow), .pin14(n74161_1_pin14[0]),
    .pin13(n74161_1_pin14[1]), .pin12(n74161_1_pin14[2]), .pin11(n74161_1_pin14[3]),
    .pin10(enableLoad_activeLow), .pin9(enableLoad_activeLow));  // open: pin15
  not not_1 (n74161_1_pin1, clear);
  buf buffer_1 (buffer_1_out, clock_1_out);
  ROM #(.addrWidth(4), .dataWidth(32)) rom_1 (
    .addr(register_1_q), .data({rom_1_data_4, rom_1_data_3, rom_1_data_2, rom_1_data}));
  Register #(.width(4)) register_1 (
    .D(n74161_1_pin14), .en(buffer_1_out), .Q(register_1_q), .clk(buffer_1_out), .clr(clear));
  Register R7 (.D(in_8), .en(clock_1_out), .Q(R7_q), .clk(clock_1_out));  // open: clr
  Register R6 (.D(in_7), .en(clock_1_out), .Q(R6_q), .clk(clock_1_out));  // open: clr
  Register R5 (.D(in_6), .en(clock_1_out), .Q(R5_q), .clk(clock_1_out));  // open: clr
  Register R4 (.D(in_5), .en(clock_1_out), .Q(R4_q), .clk(clock_1_out));  // open: clr
  OpcodeDecoder opcodedecoder_1 (
    .Opcode(rom_1_data_4), .ADD(opcodedecoder_1_add), .SUB(opcodedecoder_1_sub), .MUL(opcodedecoder_1_mul),
    .DIV(opcodedecoder_1_div), .MODx(opcodedecoder_1_modx), .NOTx(opcodedecoder_1_notx),
    .ANDx(opcodedecoder_1_andx), .ORx(opcodedecoder_1_orx), .XORx(opcodedecoder_1_xorx),
    .EQ(opcodedecoder_1_eq), .NEQ(opcodedecoder_1_neq), .GTE(opcodedecoder_1_gte), .LTE(opcodedecoder_1_lte),
    .GT(opcodedecoder_1_gt), .LT(opcodedecoder_1_lt));  // open: NOP, JMP, JMPi, JMPT, JMPTi, SET, COPY, LOAD, LOADi, STR, STRi, PUSH, POP
  Register R3 (.D(in_4), .en(clock_1_out), .Q(R3_q), .clk(clock_1_out));  // open: clr
  Register R2 (.D(in_3), .en(clock_1_out), .Q(R2_q), .clk(clock_1_out));  // open: clr
  Register R1 (.D(in_2), .en(clock_1_out), .Q(R1_q), .clk(clock_1_out));  // open: clr
  Register R0 (.D(in_1), .en(clock_1_out), .Q(R0_q), .clk(clock_1_out));  // open: clr
  Multiplexer #(.select(3), .width(8)) multiplexer_1 (
    .in0(R0_q), .in1(R1_q), .in2(R2_q), .in3(R3_q), .in4(R4_q), .in5(R5_q), .in6(R6_q), .in7(R7_q),
    .out({multiplexer_1_out_2, multiplexer_1_out}), .sel(rom_1_data[2:0]));
  Multiplexer #(.select(3), .width(8)) multiplexer_2 (
    .in0(R0_q), .in1(R1_q), .in2(R2_q), .in3(R3_q), .in4(R4_q), .in5(R5_q), .in6(R6_q), .in7(R7_q),
    .out({multiplexer_2_out_2, multiplexer_2_out}), .sel(rom_1_data_2[2:0]));
  Multiplexer #(.select(3), .width(8)) multiplexer_3 (
    .in0(R0_q), .in1(R1_q), .in2(R2_q), .in3(R3_q), .in4(R4_q), .in5(R5_q), .in6(R6_q), .in7(R7_q),
    .out(multiplexer_3_out), .sel(rom_1_data_3[2:0]));
  ALU alu_1 (
    .A({multiplexer_2_out_2, multiplexer_2_out}), .B({multiplexer_1_out_2, multiplexer_1_out}),
    .ADD(opcodedecoder_1_add), .SUB(opcodedecoder_1_sub), .MUL(opcodedecoder_1_mul),
    .DIV(opcodedecoder_1_div), .MODx(opcodedecoder_1_modx), .NOTx(opcodedecoder_1_notx),
    .ANDx(opcodedecoder_1_andx), .ORx(opcodedecoder_1_orx), .XORx(opcodedecoder_1_xorx),
    .EQ(opcodedecoder_1_eq), .NEQ(opcodedecoder_1_neq), .GTE(opcodedecoder_1_gte), .LTE(opcodedecoder_1_lte),
    .GT(opcodedecoder_1_gt), .LT(opcodedecoder_1_lt), .Result(alu_1_result));
  Hex_Digit_Display hex_digit_display_1 (.value(alu_1_result[7:4]));  // open: dp
  Hex_Digit_Display hex_digit_display_2 (.value(alu_1_result[3:0]));  // open: dp
  Hex_Digit_Display hex_digit_display_3 (.value(multiplexer_1_out));  // open: dp
  Hex_Digit_Display hex_digit_display_4 (.value(multiplexer_2_out));  // open: dp
  Hex_Digit_Display hex_digit_display_5 (.value(multiplexer_3_out[3:0]));  // open: dp

  // Notes on the sheet:
  //   contents of rom_1 (hex, n*v repeats v):
  //   10010203 10040506 10070007 10010102
  //   RC
  //   RB
  //   RA
endmodule
